// Digital circuit CPU.dig as structural Verilog
module CPU (
);

  wire alu_1_c0, alu_1_c1, alu_1_c2, alu_1_c3, alu_1_c4, alu_1_c5, alu_1_c6, alu_1_c7, alu_1_cout, alu_1_eq,
       alu_1_z, decode_1_halt, decode_1_inc, decode_1_mem_ein, decode_1_mem_eout, decode_1_memah_ein,
       decode_1_memal_ein, decode_1_p0, decode_1_p1, decode_1_p2, decode_1_pc_ein, decode_1_pc_eout,
       decode_1_pg, decode_1_regc_ein, decode_1_regc_eout, decode_1_regf1_ein, decode_1_regf1_eout,
       decode_1_regf2_ein, decode_1_regf2_eout, decode_1_regs2_ein, decode_1_regs2_eout, decode_1_rst,
       decode_1_s0, decode_1_s1, decode_1_s2, decode_1_s3, decode_1_stk_eout, pulldown_25_out,
       pulldown_26_out, pulldown_27_out, REG_A_p1, REG_A_p2, REG_A_p3, REG_A_p4, REG_A_p5, REG_A_p6,
       REG_A_p7, REG_A_p8, REG_A_p11, REG_A_p12, REG_A_p13, REG_A_p14, REG_A_p15, REG_A_p16, REG_A_p17,
       REG_A_p18, REG_A_p19, REG_A_p20, REG_B_p11, REG_B_p12, REG_B_p13, REG_B_p14, REG_B_p15, REG_B_p16,
       REG_B_p17, REG_B_p18, REG_B_p19, REG_B_p20, REG_C_m0, REG_C_m1, REG_C_m2, REG_C_m3, REG_C_m4,
       REG_C_m5, REG_C_m6, REG_C_m7, REG_F1_m0, REG_F1_m1, REG_F1_m2, REG_F1_m3, REG_F2_m0, REG_F2_m1,
       REG_F2_m2, REG_F2_m3, REG_S1_p11, REG_S1_p12, REG_S1_p13, REG_S1_p14, REG_S1_p15, REG_S1_p16,
       REG_S1_p17, REG_S1_p18, REG_S1_p19, REG_S1_p20, REG_S2_m0, REG_S2_m1, REG_S2_m2, REG_S2_m3, rom_1_p12,
       rom_1_p13, rom_1_p30, rom_1_p31, rom_1_p32, rom_1_p33, rom_1_p34, rom_1_p35, rom_1_p36, rom_1_p37,
       undriven, undriven_3, undriven_4;
  wire [3:0] pc_1_a0, pc_1_a4, pc_1_a8, pc_1_a12, pulldown_20_out, pulldown_24_out, rom_1_p7, rom_1_p11,
       rom_1_p16, rom_1_p18;
  wire [7:0] undriven_2;

  PC pc_1 (
    .D7(pulldown_20_out[3]), .D6(pulldown_20_out[2]), .D5(pulldown_20_out[1]), .D4(pulldown_20_out[0]),
    .D3(pulldown_24_out[3]), .D2(pulldown_24_out[2]), .D1(pulldown_24_out[1]), .D0(pulldown_24_out[0]),
    .A7(pc_1_a4[3]), .A6(pc_1_a4[2]), .A5(pc_1_a4[1]), .A4(pc_1_a4[0]), .A3(pc_1_a0[3]), .A2(pc_1_a0[2]),
    .A1(pc_1_a0[1]), .A0(pc_1_a0[0]), .A8(pc_1_a8[0]), .A9(pc_1_a8[1]), .A10(pc_1_a8[2]), .A11(pc_1_a8[3]),
    .A12(pc_1_a12[0]), .A13(pc_1_a12[1]), .A14(pc_1_a12[2]), .A15(pc_1_a12[3]));
  LED A14 (.in(pc_1_a12[2]));
  LED A15 (.in(pc_1_a12[3]));
  PullDown pulldown_1 (.out(pc_1_a12[2]));
  PullDown pulldown_2 (.out(pc_1_a12[3]));
  Seven_Seg_Hex seven_seg_hex_1 (.d(pc_1_a12), .dp(1'b0));
  LED A12 (.in(pc_1_a12[0]));
  LED A13 (.in(pc_1_a12[1]));
  PullDown pulldown_3 (.out(pc_1_a12[0]));
  PullDown pulldown_4 (.out(pc_1_a12[1]));
  Seven_Seg_Hex seven_seg_hex_2 (.d(pc_1_a8), .dp(1'b0));
  LED A10 (.in(pc_1_a8[2]));
  LED A11 (.in(pc_1_a8[3]));
  PullDown pulldown_5 (.out(pc_1_a8[2]));
  PullDown pulldown_6 (.out(pc_1_a8[3]));
  Seven_Seg_Hex seven_seg_hex_3 (.d(pc_1_a4), .dp(1'b0));
  LED A8 (.in(pc_1_a8[0]));
  LED A9 (.in(pc_1_a8[1]));
  PullDown pulldown_7 (.out(pc_1_a8[0]));
  PullDown pulldown_8 (.out(pc_1_a8[1]));
  Seven_Seg_Hex seven_seg_hex_4 (.d(pc_1_a0), .dp(1'b0));
  LED A6 (.in(pc_1_a4[2]));
  LED A7 (.in(pc_1_a4[3]));
  PullDown pulldown_9 (.out(pc_1_a4[3]));
  PullDown pulldown_10 (.out(pc_1_a4[2]));
  LED A4 (.in(pc_1_a4[0]));
  LED A5 (.in(pc_1_a4[1]));
  PullDown pulldown_11 (.out(pc_1_a4[1]));
  PullDown pulldown_12 (.out(pc_1_a4[0]));
  LED A2 (.in(pc_1_a0[2]));
  LED A3 (.in(pc_1_a0[3]));
  PullDown pulldown_13 (.out(pc_1_a0[3]));
  PullDown pulldown_14 (.out(pc_1_a0[2]));
  LED A0 (.in(pc_1_a0[0]));
  LED A1 (.in(pc_1_a0[1]));
  PullDown pulldown_15 (.out(pc_1_a0[1]));
  PullDown pulldown_16 (.out(pc_1_a0[0]));
  LED D7 (.in(pulldown_20_out[3]));
  PullDown pulldown_17 (.out(pulldown_20_out[3]));
  Seven_Seg_Hex seven_seg_hex_5 (.d(pulldown_20_out), .dp(1'b0));
  LED D5 (.in(pulldown_20_out[1]));
  LED D6 (.in(pulldown_20_out[2]));
  PullDown pulldown_18 (.out(pulldown_20_out[2]));
  PullDown pulldown_19 (.out(pulldown_20_out[1]));
  Seven_Seg_Hex seven_seg_hex_6 (.d(pulldown_24_out), .dp(1'b0));
  LED D3 (.in(pulldown_24_out[3]));
  LED D4 (.in(pulldown_20_out[0]));
  PullDown pulldown_20 (.out(pulldown_20_out[0]));
  PullDown pulldown_21 (.out(pulldown_24_out[3]));
  LED D1 (.in(pulldown_24_out[1]));
  LED D2 (.in(pulldown_24_out[2]));
  PullDown pulldown_22 (.out(pulldown_24_out[2]));
  PullDown pulldown_23 (.out(pulldown_24_out[1]));
  LED D0 (.in(pulldown_24_out[0]));
  PullDown pulldown_24 (.out(pulldown_24_out[0]));
  LED ENABLE (.in(undriven_4));
  LED LOAD (.in(pulldown_25_out));
  PullDown pulldown_25 (.out(pulldown_25_out));
  LED CLK (.in(pulldown_26_out));
  LED RST (.in(pulldown_27_out));
  PullDown pulldown_26 (.out(pulldown_26_out));
  PullDown pulldown_27 (.out(pulldown_27_out));
  Seven_Seg_Hex seven_seg_hex_7 (.d(rom_1_p7), .dp(1'b0));
  LED A7_2 (.in(rom_1_p7[3]));
  LED A6_2 (.in(rom_1_p7[2]));
  // Register8 REG_A: pin names not known; wires that end beside it: REG_A_p1, REG_A_p2, REG_A_p3, REG_A_p4, REG_A_p5, REG_A_p6, REG_A_p7, REG_A_p8, pulldown_25_out, pulldown_27_out, REG_A_p11, REG_A_p12, REG_A_p13, REG_A_p14, REG_A_p15, REG_A_p16, REG_A_p17, REG_A_p18, REG_A_p19, REG_A_p20
  // Register8 REG_B: pin names not known; wires that end beside it: REG_A_p1, REG_A_p2, REG_A_p3, REG_A_p4, REG_A_p5, REG_A_p6, REG_A_p7, REG_A_p8, pulldown_25_out, pulldown_27_out, REG_B_p11, REG_B_p12, REG_B_p13, REG_B_p14, REG_B_p15, REG_B_p16, REG_B_p17, REG_B_p18, REG_B_p19, REG_B_p20
  // Register8 REG_S1: pin names not known; wires that end beside it: REG_A_p1, REG_A_p2, REG_A_p3, REG_A_p4, REG_A_p5, REG_A_p6, REG_A_p7, REG_A_p8, pulldown_25_out, pulldown_27_out, REG_S1_p11, REG_S1_p12, REG_S1_p13, REG_S1_p14, REG_S1_p15, REG_S1_p16, REG_S1_p17, REG_S1_p18, REG_S1_p19, REG_S1_p20
  Register4 REG_S2 (
    .D3(REG_A_p5), .D2(REG_A_p6), .D1(REG_A_p7), .D0(REG_A_p8), .LOAD(pulldown_25_out),
    .RST(pulldown_27_out), .EOUT(decode_1_regs2_eout), .EIN(decode_1_regs2_ein), .M0(REG_S2_m0),
    .M1(REG_S2_m1), .M2(REG_S2_m2), .M3(REG_S2_m3));
  Seven_Seg_Hex seven_seg_hex_8 (.d(rom_1_p11), .dp(1'b0));
  LED A5_2 (.in(rom_1_p7[1]));
  LED A4_2 (.in(rom_1_p7[0]));
  LED M7 (.in(REG_A_p20));
  LED M7_2 (.in(REG_B_p20));
  LED M7_3 (.in(REG_S1_p20));
  LED M3 (.in(REG_S2_m3));
  MemoryManager memorymanager_1 (
    .D7(REG_A_p1), .D6(REG_A_p2), .D5(REG_A_p3), .D4(REG_A_p4), .D3(REG_A_p5), .D2(REG_A_p6), .D1(REG_A_p7),
    .D0(REG_A_p8), .EIN_L(decode_1_memal_ein), .LOAD(pulldown_25_out), .RST(pulldown_27_out),
    .EIN_H(decode_1_memah_ein), .EOUT(decode_1_mem_eout), .EIN(decode_1_mem_ein), .PG(decode_1_pg),
    .P2(decode_1_p2), .INC(decode_1_inc), .P1(decode_1_p1), .P0(decode_1_p0));  // open: A7, A6, A5, A4, A3, A2, A1, A0
  LED A3_2 (.in(rom_1_p11[3]));
  LED A2_2 (.in(rom_1_p11[2]));
  LED M6 (.in(REG_A_p19));
  LED M5 (.in(REG_A_p18));
  LED M6_2 (.in(REG_B_p19));
  LED M5_2 (.in(REG_B_p18));
  LED M6_3 (.in(REG_S1_p19));
  LED F (.in(REG_S1_p18));
  LED M2 (.in(REG_S2_m2));
  LED M1 (.in(REG_S2_m1));
  LED A1_2 (.in(rom_1_p11[1]));
  LED A0_2 (.in(rom_1_p11[0]));
  // ROM rom_1: pin names not known; wires that end beside it: rom_1_p7[3], rom_1_p7[2], rom_1_p7[1], rom_1_p7[3], rom_1_p7[2], rom_1_p7[1], rom_1_p7[0], rom_1_p11[3], rom_1_p11[2], rom_1_p11[1], rom_1_p11[0], rom_1_p12, rom_1_p13, rom_1_p16[3], rom_1_p16[2], rom_1_p16[1], rom_1_p16[0], rom_1_p18[3], rom_1_p18[2], rom_1_p18[1], rom_1_p18[0], REG_A_p1, REG_A_p2, REG_A_p3, REG_A_p4, REG_A_p5, REG_A_p6, REG_A_p7, REG_A_p8, rom_1_p30, rom_1_p31, rom_1_p32, rom_1_p33, rom_1_p34, rom_1_p35, rom_1_p36, rom_1_p37
  LED M4 (.in(REG_A_p17));
  LED M3_2 (.in(REG_A_p16));
  LED M4_2 (.in(REG_B_p17));
  LED M3_3 (.in(REG_B_p16));
  LED M (.in(REG_S1_p17));
  LED S3 (.in(REG_S1_p16));
  LED CIN (.in(REG_S2_m0));
  LED M2_2 (.in(REG_A_p15));
  LED M1_2 (.in(REG_A_p14));
  LED M2_3 (.in(REG_B_p15));
  LED M1_3 (.in(REG_B_p14));
  LED S1 (.in(REG_S1_p14));
  LED S2 (.in(REG_S1_p15));
  LED M0 (.in(REG_A_p13));
  LED M0_2 (.in(REG_B_p13));
  LED S0 (.in(REG_S1_p13));
  Seven_Seg_Hex seven_seg_hex_9 (.d(rom_1_p16), .dp(1'b0));
  Seven_Seg_Hex seven_seg_hex_10 (.d(rom_1_p18), .dp(1'b0));
  ALU alu_1 (
    .A0(REG_A_p13), .A1(REG_A_p14), .A2(REG_A_p15), .A3(REG_A_p16), .A4(REG_A_p17), .A5(REG_A_p18),
    .A6(REG_A_p19), .A7(REG_A_p20), .B0(REG_B_p13), .B1(REG_B_p14), .B2(REG_B_p15), .B3(REG_B_p16),
    .B4(REG_B_p17), .B5(REG_B_p18), .B6(REG_B_p19), .B7(REG_B_p20), .S0(REG_S1_p13), .S1(REG_S1_p14),
    .S2(REG_S1_p15), .S3(REG_S1_p16), .M(REG_S1_p17), .CIN(REG_S2_m0), .F(REG_S1_p18), .C0(alu_1_c0),
    .C1(alu_1_c1), .C2(alu_1_c2), .C3(alu_1_c3), .C4(alu_1_c4), .C5(alu_1_c5), .C6(alu_1_c6), .C7(alu_1_c7),
    .Z(alu_1_z), .EQ(alu_1_eq), .COUT(alu_1_cout));
  LED C7 (.in(alu_1_c7));
  LED C6 (.in(alu_1_c6));
  LED C5 (.in(alu_1_c5));
  LED C4 (.in(alu_1_c4));
  Seven_Seg_Hex seven_seg_hex_11 (.d(undriven_2[7:4]), .dp(1'b0));
  DECODE decode_1 (
    .A7(rom_1_p16[3]), .A6(rom_1_p16[2]), .A5(rom_1_p16[1]), .A4(rom_1_p16[0]), .A3(rom_1_p18[3]),
    .A2(rom_1_p18[2]), .A1(rom_1_p18[1]), .A0(rom_1_p18[0]), .ROM_EDOUT(rom_1_p12), .PC_EIN(decode_1_pc_ein),
    .REGF2_EOUT(decode_1_regf2_eout), .REGF2_EIN(decode_1_regf2_ein), .REGF1_EOUT(decode_1_regf1_eout),
    .REGF1_EIN(decode_1_regf1_ein), .REGS2_EOUT(decode_1_regs2_eout), .REGS2_EIN(decode_1_regs2_ein),
    .PC_EOUT(decode_1_pc_eout), .ROM_EAOUT(rom_1_p13), .STK_EOUT(decode_1_stk_eout),
    .MEMAH_EIN(decode_1_memah_ein), .MEMAL_EIN(decode_1_memal_ein), .MEM_EOUT(decode_1_mem_eout),
    .MEM_EIN(decode_1_mem_ein), .REGS1_EOUT(REG_S1_p11), .REGS1_EIN(REG_S1_p12),
    .REGC_EOUT(decode_1_regc_eout), .REGC_EIN(decode_1_regc_ein), .REGB_EOUT(REG_B_p11),
    .REGB_EIN(REG_B_p12), .REGA_EOUT(REG_A_p11), .REGA_EIN(REG_A_p12), .C(REG_F2_m0), .Z(REG_F1_m0),
    .EQ(REG_F1_m1), .SWP(undriven), .S0(decode_1_s0), .S1(decode_1_s1), .S2(decode_1_s2), .RST(decode_1_rst),
    .ENABLE(undriven_4), .P0(decode_1_p0), .P1(decode_1_p1), .P2(decode_1_p2), .PG(decode_1_pg),
    .INC(decode_1_inc), .S3(decode_1_s3), .HALT(decode_1_halt), .SPARE4(undriven_2), .NEG(1'b0), .OVR(1'b0),
    .IRQ(undriven_3), .SPARE1(1'b0), .SPARE2(1'b0), .SPARE3(1'b0));  // open: IV_EIN, IV_EOUT, IRQ_ON, IRQ_OFF, IRQ_SUP_ON, IRQ_SUP_OFF
  LED C3 (.in(alu_1_c3));
  LED C2 (.in(alu_1_c2));
  Seven_Seg_Hex seven_seg_hex_12 (.d(undriven_2[3:0]), .dp(1'b0));
  LED C1 (.in(alu_1_c1));
  LED C0 (.in(alu_1_c0));
  LED Z (.in(alu_1_z));
  LED COUT (.in(alu_1_cout));
  LED EQ (.in(alu_1_eq));
  Register_SepOut8 REG_C (
    .D7(alu_1_c7), .D6(alu_1_c6), .D5(alu_1_c5), .D4(alu_1_c4), .D3(alu_1_c3), .D2(alu_1_c2), .D1(alu_1_c1),
    .D0(alu_1_c0), .LOAD(pulldown_25_out), .RST(pulldown_27_out), .EOUT(decode_1_regc_eout),
    .EIN(decode_1_regc_ein), .M0(REG_C_m0), .M1(REG_C_m1), .M2(REG_C_m2), .M3(REG_C_m3), .M4(REG_C_m4),
    .M5(REG_C_m5), .M6(REG_C_m6), .M7(REG_C_m7), .Q7(REG_A_p1), .Q6(REG_A_p2), .Q5(REG_A_p3), .Q4(REG_A_p4),
    .Q3(REG_A_p5), .Q2(REG_A_p6), .Q1(REG_A_p7), .Q0(REG_A_p8));
  Register_SepOut4 REG_F1 (
    .D3(1'b0), .D2(1'b0), .D1(alu_1_eq), .D0(alu_1_z), .LOAD(pulldown_25_out), .RST(pulldown_27_out),
    .EOUT(decode_1_regf1_eout), .EIN(decode_1_regf1_ein), .M0(REG_F1_m0), .M1(REG_F1_m1), .M2(REG_F1_m2),
    .M3(REG_F1_m3), .Q3(REG_A_p5), .Q2(REG_A_p6), .Q1(REG_A_p7), .Q0(REG_A_p8));
  Register_SepOut4 REG_F2 (
    .D3(1'b0), .D2(1'b0), .D1(1'b0), .D0(alu_1_cout), .LOAD(pulldown_25_out), .RST(pulldown_27_out),
    .EOUT(decode_1_regf2_eout), .EIN(decode_1_regf2_ein), .M0(REG_F2_m0), .M1(REG_F2_m1), .M2(REG_F2_m2),
    .M3(REG_F2_m3), .Q3(REG_A_p5), .Q2(REG_A_p6), .Q1(REG_A_p7), .Q0(REG_A_p8));
  LED M7_4 (.in(REG_C_m7));
  LED M6_4 (.in(REG_C_m6));
  LED M3_4 (.in(REG_F1_m3));
  LED M2_4 (.in(REG_F1_m2));
  LED M3_5 (.in(REG_F2_m3));
  LED M2_5 (.in(REG_F2_m2));
  LED M5_3 (.in(REG_C_m5));
  LED M4_3 (.in(REG_C_m4));
  LED EQ_2 (.in(REG_F1_m1));
  LED Z_2 (.in(REG_F1_m0));
  LED M1_4 (.in(REG_F2_m1));
  LED COUT_2 (.in(REG_F2_m0));
  LED M3_6 (.in(REG_C_m3));
  LED M2_6 (.in(REG_C_m2));
  LED M1_5 (.in(REG_C_m1));
  LED M0_3 (.in(REG_C_m0));

  // Notes on the sheet:
  //   Address
  //   Data
  //   Instruction
  //   Address
  //   Instruction
  //   Actual Instruction
endmodule
